# Fritzing sketch Wiring Diagram (saved by Fritzing 0.9.5d)

parts:
  MCU1 = Raspberry Pi Zero
  D1 = Diode [package=sot23-3]
  Mod1 = KY-021 Mini Magnetic Reed Switch Module [package="Breakout board"]
  Mod2 = KY-021 Mini Magnetic Reed Switch Module [package="Breakout board"]

nets:
  N1: MCU1.pin_1, MCU1.pin_17, Mod1.-, Mod2.-
  N2: MCU1.pin_9, MCU1.pin_39, D1.C
  N3: MCU1.pin_11, Mod1.S
  N4: MCU1.pin_15, Mod2.S
  N5: MCU1.pin_37, D1.A

custom parts:
  KY-021 Mini Magnetic Reed Switch Module: KY-021 magnetic reed switch module. A reed switch is a magnetic sensor that is normally open and gets closed when exposed to a magnetic field.
